# Fritzing sketch Connections Sketch (saved by Fritzing 0.9.3b)
breadboards: 1

parts:
  Raspberry_Pi1 = Raspberry Pi 2
  J1 = Basic Servo
  J2 = Basic Servo
  J3 = Basic Servo
  J4 = Basic Servo
  J5 = Basic Servo
  J6 = Basic Servo
  J7 = Basic Servo

nets:
  N1: Raspberry_Pi1.GPIO2, J1.pulse
  N2: Raspberry_Pi1.GPIO3, J3.pulse
  N3: Raspberry_Pi1.GPIO4, J2.pulse
  GND: Raspberry_Pi1.GND, J1.gnd, J2.gnd, J3.gnd, J4.gnd, J5.gnd, J6.gnd, J7.gnd
  N4: Raspberry_Pi1.GPIO23, J4.pulse
  N5: Raspberry_Pi1.GPIO18, J5.pulse
  N6: Raspberry_Pi1.GPIO15, J6.pulse
  N7: Raspberry_Pi1.GPIO14, J7.pulse
  VCC: Raspberry_Pi1.5V, J1.vcc, J2.vcc, J3.vcc, J4.vcc, J5.vcc, J6.vcc, J7.vcc
